// Logisim project DESLOCAMENTO FRAGMENTADO.circ as structural Verilog: 1 circuit, main circuit main
// DESLOC
module main (
  input  D_3,
  input  D_2,
  input  D_1,
  input  D_0,
  input  S_0,
  input  S_1,
  input  S1,
  input  S1_2,
  input  NOT_S1,
  input  NOT_S1_2,
  input  NOT_S1_3,
  input  DY_MEIO,
  input  YD_ANTERIOR,
  input  YD_ANTERIOR_2,
  input  YD_PROXIMO,
  input  YD_PROXIMO_2,
  input  DY_MEIO_2,
  output S1_3,
  output S1_4,
  output S1_5,
  output NOT_S1_4,
  output NOT_S1_5,
  output NOT_S1_6,
  output DY_PROXIMO,
  output DY_PROXIMO_2,
  output DY_PROXIMO_3,
  output DY_MEIO_3,
  output DY_ANTERIOR,
  output DY_ANTERIOR_2,
  output Q_3,
  output Q_2,
  output Q_1,
  output Q_0
);

  wire _1_out;

  not _11 (NOT_S1_4, S_1);
  and _2 (DY_MEIO_3, D_3, S_1);
  and _1 (_1_out, S_1, S_0, D_3);
  or _8 (Q_3, _1_out, DY_MEIO);
  and _4 (DY_ANTERIOR, D_2, S1);
  and _3 (DY_PROXIMO, NOT_S1, D_2);
  or _9 (Q_2, YD_PROXIMO, YD_ANTERIOR);
  and _5 (DY_PROXIMO_2, NOT_S1_2, D_1);
  or _10 (Q_1, YD_PROXIMO_2, YD_ANTERIOR_2);
  and _6 (DY_ANTERIOR_2, D_1, S1_2);
  and _7 (DY_PROXIMO_3, NOT_S1_3, D_0);

  assign NOT_S1_5 = NOT_S1;
  assign NOT_S1_6 = NOT_S1_2;
  assign Q_0 = DY_MEIO_2;
  assign S1_3 = S_1;
  assign S1_4 = S1;
  assign S1_5 = S1_2;
endmodule
