// Logisim project MEIO SOMADOR HA.circ as structural Verilog
module main (
  input  A,
  input  B,
  output Q,
  output Cout
);

  xor XOR (Q, A, B);
  and AND (Cout, B, A);
endmodule
