// Logisim project MUX 2 x 1 NEGADO.circ as structural Verilog: 1 circuit, main circuit main
module main (
  input  S,
  input  S_2,
  input  E_1,
  input  E_1_2,
  input  E_2,
  input  E_2_2,
  output Y,
  output Y_2
);

  wire _1_2_out, _1_out, _2_2_out, _2_out, _3_2_out, _3_out;

  not _1 (_1_out, S);
  and _2 (_2_out, _1_out, E_1);
  and _3 (_3_out, S, E_2);
  or _4 (Y, _2_out, _3_out);
  not _1_2 (_1_2_out, S_2);
  nand _2_2 (_2_2_out, _1_2_out, E_1_2);
  nand _3_2 (_3_2_out, S_2, E_2_2);
  nand _4_2 (Y_2, _2_2_out, _3_2_out);
endmodule
