// Logisim project NEGAÇÃO COMPARADOR[.circ as structural Verilog: 1 circuit, main circuit main
module main (
  input  Q0,
  input  Q1,
  input  Q2,
  input  Q3,
  input  Q4,
  input  Q5,
  input  Q6,
  input  Q7,
  input  Q8,
  input  Q9,
  input  Cout,
  input  C_8,
  input  A_0,
  input  A_1,
  input  A_2,
  input  A_3,
  input  A_4,
  input  A_5,
  input  A_6,
  input  A_7,
  input  A_8,
  input  A_9,
  input  B_0,
  input  B_1,
  input  B_2,
  input  B_3,
  input  B_4,
  input  B_5,
  input  B_6,
  input  B_7,
  input  B_8,
  input  B_9,
  output OVER_FLOW,
  output A___B,
  output A___0,
  output A___B_2,
  output B___0,
  output A___B_3
);

  wire _4_out, _5_out, _6_out, _9_out, _10_out, _11_out;

  nor _1 (A___B, Q0, Q1, Q2, Q3, Q4, Q5, Q6, Q7, Q8, Q9);
  nor _2 (A___0, A_0, A_1, A_2, A_3, A_4, A_5, A_6, A_7, A_8, A_9);
  nor _3 (B___0, B_0, B_1, B_2, B_3, B_4, B_5, B_6, B_7, B_8, B_9);
  not _10 (_10_out, A___B);
  xnor _9 (_9_out, A_9, B_9);
  not _11 (_11_out, A_9);
  nand _4 (_4_out, Cout, _10_out, _9_out);
  nand _5 (_5_out, _10_out, _11_out, B_9);
  nand _6 (_6_out, _10_out, _11_out, B___0);
  nand _7 (A___B_3, A___B_2, A___B);
  xor _10_2 (OVER_FLOW, C_8, Cout);
  nand _8 (A___B_2, _4_out, _5_out, _6_out);
endmodule
