// Logisim project NEGAÇÃO DESLOCAMENTO.circ as structural Verilog: 1 circuit, main circuit main
module main (
  input  S0,
  input  D9,
  input  D8,
  input  D7,
  input  D6,
  input  D5,
  input  D4,
  input  D3,
  input  D2,
  input  D1,
  input  D0,
  input  S1,
  output Q9,
  output Q8,
  output Q7,
  output Q6,
  output Q5,
  output Q4,
  output Q3,
  output Q2,
  output Q1,
  output Q0
);

  wire _1_out, _2_out, _3_out, _4_out, _5_out, _6_out, _7_out, _8_out, _9_out, _10_out, _11_out, _12_out,
       _13_out, _14_out, _15_out, _16_out, _17_out, _18_out, _19_out, not_1_out;

  not not_1 (not_1_out, S1);
  nor _1 (_1_out, not_1_out, S0, D9);
  nor _2 (_2_out, D9, not_1_out);
  nor _20 (Q9, _1_out, _3_out);
  nor _4 (_4_out, D8, not_1_out);
  nor _3 (_3_out, S1, D8);
  nor _21 (Q8, _2_out, _5_out);
  nor _5 (_5_out, S1, D7);
  nor _22 (Q7, _4_out, _7_out);
  nor _7 (_7_out, S1, D6);
  nor _6 (_6_out, D7, not_1_out);
  nor _8 (_8_out, D6, not_1_out);
  nor _23 (Q6, _6_out, _9_out);
  nor _10 (_10_out, D5, not_1_out);
  nor _9 (_9_out, S1, D5);
  nor _24 (Q5, _8_out, _11_out);
  nor _11 (_11_out, S1, D4);
  nor _12 (_12_out, D4, not_1_out);
  nor _25 (Q4, _10_out, _13_out);
  nor _13 (_13_out, S1, D3);
  nor _26 (Q3, _12_out, _15_out);
  nor _14 (_14_out, D3, not_1_out);
  nor _15 (_15_out, S1, D2);
  nor _16 (_16_out, D2, not_1_out);
  nor _27 (Q2, _14_out, _17_out);
  nor _18 (_18_out, D1, not_1_out);
  nor _17 (_17_out, S1, D1);
  nor _28 (Q1, _16_out, _19_out);
  nor _19 (_19_out, S1, D0);
  not not_2 (Q0, _18_out);
endmodule
