// Logisim project NEGAÇÃO SST.circ as structural Verilog: 1 circuit, main circuit main
// SST
module main (
  input  Cin,
  input  S,
  input  A,
  input  B,
  output Q,
  output Cout
);

  wire _1_out, _2_out, nand_1_out, nand_2_out;

  xor _1 (_1_out, S, B);
  xor _2 (_2_out, A, _1_out);
  nand nand_1 (nand_1_out, _1_out, A);
  nand nand_2 (nand_2_out, Cin, _2_out);
  xor _3 (Q, _2_out, Cin);
  nand nand_3 (Cout, nand_2_out, nand_1_out);
endmodule
