// Logisim project PORTAS E MULTIPLEXADOR.circ as structural Verilog: 1 circuit, main circuit main
module main (
  input  A,
  input  A_2,
  input  B,
  input  B_2,
  input  A_3,
  input  A_4,
  input  B_3,
  input  B_4,
  input  A_5,
  input  A_6,
  input  B_5,
  input  B_6,
  input  S,
  input  A_7,
  input  A_8,
  input  B_7,
  output Y,
  output Y_2,
  output Y_3,
  output Y_4,
  output Y_5,
  output Y_6,
  output Y_7,
  output Y_8
);

  and AND (Y, A, B);
  or OR (Y_3, A_3, B_3);
  xor XOR (Y_5, A_5, B_5);
  Multiplexer #(.enable("false")) multiplexer_1 (.in0(A_8), .in1(B_7), .out(Y_8), .sel(S));
  nand NAND (Y_2, A_2, B_2);
  nor NOR (Y_4, A_4, B_4);
  xnor XNOR (Y_6, A_6, B_6);
  not NOT (Y_7, A_7);
endmodule
