// Logisim project PORTAS LÓGICAS COMPOSTAS POR TRANSISTORES.circ as structural Verilog: 1 circuit, main circuit main
module main (
  input  A,
  input  A_2,
  input  A_3,
  input  A_4,
  input  B,
  input  B_2,
  input  A_5,
  input  A_6,
  input  A_7,
  input  A_8,
  input  B_3,
  input  B_4,
  input  B_5,
  input  B_6,
  input  A_9,
  input  A_10,
  input  B_7,
  input  B_8,
  input  A_11,
  input  A_12,
  input  B_9,
  input  B_10,
  input  in_23,
  input  in_24,
  input  in_25,
  input  in_26,
  output Y,
  output Y_2,
  output Y_3,
  output Y_4,
  output Y_5,
  output Y_6,
  output Y_7,
  output Y_8,
  output S,
  output Y_9,
  output S_2,
  output Y_10,
  output out_39,
  output out_40
);

  wire not_1_out, transistor_3_out, transistor_6_out, transistor_7_out, transistor_8_out, transistor_11_out,
       transistor_26_out, transistor_30_out, transistor_31_out;

  not not_1 (not_1_out, in_24);
  Transistor transistor_1 (.in(1'b1), .out(Y), .gate(A_3));
  Transistor #(.\type ("n")) transistor_2 (.in(1'b0), .out(Y), .gate(A_3));
  Transistor transistor_3 (.in(1'b1), .out(transistor_3_out), .gate(A_5));
  Transistor transistor_4 (.in(1'b1), .out(transistor_3_out), .gate(B_4));
  Transistor #(.\type ("n")) transistor_5 (.in(transistor_6_out), .out(transistor_3_out), .gate(A_5));
  Transistor #(.\type ("n")) transistor_6 (.in(1'b0), .out(transistor_6_out), .gate(B_4));
  Transistor transistor_7 (.in(1'b1), .out(transistor_7_out), .gate(A_9));
  Transistor transistor_8 (.in(transistor_7_out), .out(transistor_8_out), .gate(B_7));
  Transistor #(.\type ("n")) transistor_9 (.in(1'b0), .out(transistor_8_out), .gate(B_7));
  Transistor #(.\type ("n")) transistor_10 (.in(1'b0), .out(transistor_8_out), .gate(A_9));
  Transistor transistor_11 (.in(in_24), .out(transistor_11_out), .gate(in_23));
  Transistor #(.\type ("n")) transistor_12 (.in(not_1_out), .out(transistor_11_out), .gate(in_23));
  Transistor transistor_13 ();  // open: in, out, gate
  Transistor transistor_14 (.in(1'b1), .out(Y_5), .gate(transistor_3_out));
  Transistor #(.\type ("n")) transistor_15 (.in(1'b0), .out(Y_5), .gate(transistor_3_out));
  Transistor transistor_16 (.in(1'b1), .out(S), .gate(transistor_8_out));
  Transistor #(.\type ("n")) transistor_17 (.in(1'b0), .out(S), .gate(transistor_8_out));
  Transistor #(.\type ("n")) transistor_18 (.in(transistor_11_out), .out(in_23), .gate(not_1_out));
  Transistor #(.gate("br")) transistor_19 (.in(out_39), .out(in_23), .gate(in_24));
  Transistor transistor_20 ();  // open: in, out, gate
  // NOT_Gate not_2 is placed but not wired
  Transistor transistor_21 ();  // open: in, out, gate
  Transistor transistor_22 ();  // open: in, out, gate
  not not_3 (Y_2, A_4);
  and AND (Y_7, A_6, B_3);
  or OR (S_2, A_12, B_10);
  // NOT_Gate not_4 is placed but not wired
  Transistor #(.gate("br")) transistor_23 (.in(A), .out(Y_3), .gate(B));
  Transistor transistor_24 (.in(B), .out(Y_3), .gate(A));
  Transistor #(.\type ("n")) transistor_25 (.in(transistor_26_out), .out(Y_3), .gate(A));
  Transistor #(.\type ("n")) transistor_26 (.in(1'b0), .out(transistor_26_out), .gate(B));
  Transistor transistor_27 (.in(1'b1), .out(Y_6), .gate(A_7));
  Transistor transistor_28 (.in(1'b1), .out(Y_6), .gate(B_6));
  Transistor #(.\type ("n")) transistor_29 (.in(transistor_30_out), .out(Y_6), .gate(A_7));
  Transistor #(.\type ("n")) transistor_30 (.in(1'b0), .out(transistor_30_out), .gate(B_6));
  Transistor transistor_31 (.in(1'b1), .out(transistor_31_out), .gate(A_10));
  Transistor transistor_32 (.in(transistor_31_out), .out(Y_10), .gate(B_8));
  Transistor #(.\type ("n")) transistor_33 (.in(1'b0), .out(Y_10), .gate(B_8));
  Transistor #(.\type ("n")) transistor_34 (.in(1'b0), .out(Y_10), .gate(A_10));
  xor xor_1 (Y_4, A_2, B_2);
  nand NAND (Y_8, A_8, B_5);
  nor NOR (Y_9, A_11, B_9);

  // Notes on the sheet:
  //   pMOS
  //   nMOS
  //   pMOS
  //   nMOS
  //   pMOS
  //   nMOS
  //   INVERSOR OU PORTA NOT
  //   PORTA AND 2 ENTRADAS
  //   PORTA OR 2 ENTRADAS
  //   pMOS
  //   nMOS
  //   pMOS
  //   nMOS
  //   PORTA XOR 2 ENTRADAS
  //   PORTA NAND 2 ENTRADAS
  //   PORTA NOR 2 ENTRADAS
endmodule
