// Logisim project SOMADOR CLA.circ as structural Verilog: 1 circuit, main circuit main
module main (
  input  Cin,
  input  A0,
  input  B0,
  input  A1,
  input  B1,
  input  A2,
  input  B2,
  output Q0,
  output Q1,
  output Q2,
  output Cout
);

  wire AND_1_out, AND_2_out, AND_3_out, AND_4_out, AND_5_out, AND_6_out, AND_7_out, AND_8_out, AND_9_out,
       OR_1_out, OR_2_out, XOR_1_out, XOR_2_out, XOR_3_out;

  xor XOR_1 (XOR_1_out, A0, B0);
  and AND_1 (AND_1_out, A0, B0);
  xor XOR_2 (XOR_2_out, A1, B1);
  and AND_2 (AND_2_out, A1, B1);
  xor XOR_3 (XOR_3_out, A2, B2);
  and AND_3 (AND_3_out, A2, B2);
  and AND_4 (AND_4_out, Cin, XOR_1_out);
  and AND_5 (AND_5_out, Cin, XOR_1_out, XOR_2_out);
  and AND_6 (AND_6_out, AND_1_out, XOR_2_out);
  and AND_7 (AND_7_out, Cin, XOR_1_out, XOR_2_out, XOR_3_out);
  and AND_8 (AND_8_out, AND_1_out, XOR_2_out, XOR_3_out);
  and AND_9 (AND_9_out, AND_2_out, XOR_3_out);
  or OR_1 (OR_1_out, AND_4_out, AND_1_out);
  or OR_2 (OR_2_out, AND_5_out, AND_2_out, AND_6_out);
  xor XOR_4 (Q0, Cin, XOR_1_out);
  xor XOR_5 (Q1, OR_1_out, XOR_2_out);
  xor XOR_6 (Q2, OR_2_out, XOR_3_out);
  or OR_3 (Cout, AND_7_out, AND_8_out, AND_9_out, AND_3_out);
endmodule
