// Logisim project TRANSISTOR E PORTA DE TRANSMISSÃO.circ as structural Verilog: 1 circuit, main circuit main
module main (
  input  Dreno,
  input  Gate,
  input  Gate_2,
  input  Source,
  input  Sinal,
  input  Entrada,
  output Dreno_2,
  output Source_2,
  output \Saída 
);

  wire transmission_1_p3;

  Transistor transistor_1 (.in(Dreno), .out(Source_2), .gate(Gate));
  // Transmission_Gate transmission_1: pin names not known; wires that end beside it: Entrada, Sinal, transmission_1_p3, \Saída 
  not not_1 (transmission_1_p3, Sinal);
  Transistor #(.\type ("n")) transistor_2 (.in(Source), .out(Dreno_2), .gate(Gate_2));

  // Notes on the sheet:
  //   pMOS
  //   Transistor
  //   Porta de transmissão
  //   nMOS
endmodule
